// Logisim project Regfile.circ as structural Verilog: 1 circuit, main circuit main
module main (
  input  [1:0] Read_register_1,
  input  [1:0] Read_register_2,
  input  [1:0] write_register,
  input  [15:0] write_data,
  input  RegWrite,
  input  clock,
  output [15:0] Reg_0_Value,
  output [15:0] Reg_1_Value,
  output [15:0] Reg_2_Value,
  output [15:0] Reg_3_Value,
  output [15:0] Read_Data_1,
  output [15:0] Read_Data_2
);

  wire [15:0] In_r0, In_r1, In_r2, In_r3;

  Register #(.width(16)) register_1 (.D(In_r0), .Q(Reg_0_Value), .clk(clock));  // open: en, clr
  Register #(.width(16)) register_2 (.D(In_r1), .Q(Reg_1_Value), .clk(clock));  // open: en, clr
  Multiplexer #(.select(2), .width(16)) multiplexer_1 (
    .in0(Reg_0_Value), .in1(Reg_1_Value), .in2(Reg_2_Value), .in3(Reg_3_Value), .out(Read_Data_1),
    .sel(Read_register_1));  // open: en
  Demultiplexer #(.select(2), .width(16), .tristate("true")) demultiplexer_1 (
    .out0(In_r0), .out1(In_r1), .out2(In_r2), .out3(In_r3), .in(write_data), .sel(write_register),
    .en(RegWrite));
  Register #(.width(16)) register_3 (.D(In_r2), .Q(Reg_2_Value), .clk(clock));  // open: en, clr
  Multiplexer #(.select(2), .width(16)) multiplexer_2 (
    .in0(Reg_0_Value), .in1(Reg_1_Value), .in2(Reg_2_Value), .in3(Reg_3_Value), .out(Read_Data_2),
    .sel(Read_register_2));  // open: en
  Register #(.width(16)) register_4 (.D(In_r3), .Q(Reg_3_Value), .clk(clock));  // open: en, clr

  // Other names for the same wires on the sheet: clk = clock; data[15:0] = write_data; r0[15:0] = Reg_0_Value;
  //   r1[15:0] = Reg_1_Value; r2[15:0] = Reg_2_Value; r3[15:0] = Reg_3_Value; reg_num[1:0] = write_register;
  //   RW = RegWrite

  // Notes on the sheet:
  //   These are INPUTS to the circuit
  //   Reg 0
  //   Reg 1
  //   These are INPUTS to the circuit
  //   DO NOT CHANGE THE LOCATIONS OF THE INPUTS/OUTPUTS! IF YOU DO SO, YOU NEED TO MAKE SURE THE PINS ARE AT THE RIGHT PLACE!
  //   These are OUTPUTS to the circuit
  //   Reg 2
  //   Yet again, the clock is not an actual clock, but an input, one that will be driven from a higher circuit
  //   Reg 3
  //   These are OUTPUTS to the circuit
endmodule
