// Logisim project alu.circ as structural Verilog: 6 circuits, main circuit main
module main (
  input  [15:0] X,
  input  [15:0] Y,
  input  [3:0] Switch__S,
  output Signed_Overflow,
  output [15:0] RESULT,
  output Equal
);

  wire comparator_1_lt;
  wire [7:0] addp8_7_0, addp8_15_8;
  wire [15:0] R_add, R_and, R_or, R_sllv, R_slt, R_srav, R_srlv, R_sub, R_subp8;

  Adder #(.width(16)) adder_1 (.a(X), .b(Y), .out(R_add));  // open: cin, cout
  Subtractor #(.width(16)) subtractor_1 (.a(X), .b(Y), .out(R_sub));  // open: bin, bout
  Comparator #(.width(16)) comparator_1 (.a(X), .b(Y), .lt(comparator_1_lt));  // open: gt, eq
  // Probe on X
  // Probe on Y
  Shifter #(.width(16)) shifter_1 (.in(X), .\dist (Y[3:0]), .out(R_sllv));
  Shifter #(.width(16), .shift("lr")) shifter_2 (.in(X), .\dist (Y[3:0]), .out(R_srlv));
  Shifter #(.width(16), .shift("ar")) shifter_3 (.in(X), .\dist (Y[3:0]), .out(R_srav));
  assign R_slt = {{15{1'b0}}, comparator_1_lt};  // Bit_Extender bit_extender_1
  Multiplexer #(.select(4), .width(16)) multiplexer_1 (
    .in0(R_add), .in1(R_sub), .in2(R_sllv), .in3(R_srlv), .in4(R_srav), .in5(R_slt), .in6(R_or), .in7(R_and),
    .in8({addp8_15_8, addp8_7_0}), .in9(R_subp8), .out(RESULT), .sel(Switch__S));  // open: in10, in11, in12, in13, in14, in15, en
  assign R_or = X | Y;  // OR_Gate or_1, 16 bits wide
  assign R_and = X & Y;  // AND_Gate and_1, 16 bits wide
  // Probe on RESULT
  Comparator #(.width(16)) comparator_2 (.a(X), .b(Y), .eq(Equal));  // open: gt, lt
  Adder adder_2 (.a(X[7:0]), .b(Y[7:0]), .out(addp8_7_0));  // open: cin, cout
  Adder adder_3 (.a(X[15:8]), .b(Y[15:8]), .out(addp8_15_8));  // open: cin, cout
  Subtractor subtractor_2 (.a(X[7:0]), .b(Y[7:0]), .out(R_subp8[7:0]));  // open: bin, bout
  Subtractor subtractor_3 (.a(X[15:8]), .b(Y[15:8]), .out(R_subp8[15:8]));  // open: bin, bout
  Signed_Overflow_Selector signed_overflow_selector_1 (
    .X(X), .Y(Y), .in_3(R_add), .in_4(R_sub), .in_5(X[7:0]), .in_6(Y[7:0]), .in_7(X[15:8]), .in_9(Y[15:8]),
    .in_10(addp8_7_0), .in_11(addp8_15_8), .in_12(R_subp8[7:0]), .in_13(R_subp8[15:8]), .Switch(Switch__S),
    .signed_overflow(Signed_Overflow));

  // Other names for the same wires on the sheet: R_addp8[15:0] = {addp8_15_8, addp8_7_0};
  //   subp8_7_0[7:0] = R_subp8[7:0]; subp8_15_8[7:0] = R_subp8[15:8]; switch[3:0] = Switch__S; X_7_0[7:0] = X[7:0];
  //   X_15_8[7:0] = X[15:8]; Y_7_0[7:0] = Y[7:0]; Y_15_8[7:0] = Y[15:8]

  // Notes on the sheet:
  //   0
  //   1
  //   2
  //   3
  //   4
  //   5
  //   INPUTS to your circuit
  //   INPUT to your circuit
  //   ARITHMETIC OPERATIONS
  //   6
  //   7
  //   8
  //   9
  //   DON'T CHANGE THE INPUTS AND OUTPUTS! IF YOU DO SO, YOU NEED TO MAKE SURE THE PINS ARE IN THE RIGHT PLACES!
  //   OUTPUTS of your circuit
  //   SIGNED OVERFLOW DETECTION
endmodule

// SO Selector
module Signed_Overflow_Selector (
  input  [15:0] X,
  input  [15:0] Y,
  input  [15:0] in_3,
  input  [15:0] in_4,
  input  [7:0] in_5,
  input  [7:0] in_6,
  input  [7:0] in_7,
  input  [3:0] Switch,
  input  [7:0] in_9,
  input  [7:0] in_10,
  input  [7:0] in_11,
  input  [7:0] in_12,
  input  [7:0] in_13,
  output signed_overflow
);

  wire or_1_out, or_2_out, signed_overflow_8bits_add_1_plus_out, signed_overflow_8bits_add_2_plus_out,
       signed_overflow_8bits_sub_1_minus_out, signed_overflow_8bits_sub_2_minus_out,
       signed_overflow_16bits_add_1_plus_out, signed_overflow_16bits_sub_1_minus_out;

  Signed_Overflow_16bits_Add signed_overflow_16bits_add_1 (
    .in_1(X), .in_2(Y), .in_3(in_3), .plus_out(signed_overflow_16bits_add_1_plus_out));
  Signed_Overflow_16bits_Sub signed_overflow_16bits_sub_1 (
    .in_1(X), .in_2(Y), .in_3(in_4), .minus_out(signed_overflow_16bits_sub_1_minus_out));
  Signed_Overflow_8bits_Add signed_overflow_8bits_add_1 (
    .in_1(in_5), .in_2(in_6), .in_3(in_10), .plus_out(signed_overflow_8bits_add_1_plus_out));
  Signed_Overflow_8bits_Add signed_overflow_8bits_add_2 (
    .in_1(in_7), .in_2(in_9), .in_3(in_11), .plus_out(signed_overflow_8bits_add_2_plus_out));
  Signed_Overflow_8bits_Sub signed_overflow_8bits_sub_1 (
    .in_1(in_5), .in_2(in_6), .in_3(in_12), .minus_out(signed_overflow_8bits_sub_1_minus_out));
  Signed_Overflow_8bits_Sub signed_overflow_8bits_sub_2 (
    .in_1(in_7), .in_2(in_9), .in_3(in_13), .minus_out(signed_overflow_8bits_sub_2_minus_out));
  or or_1 (or_1_out, signed_overflow_8bits_add_1_plus_out, signed_overflow_8bits_add_2_plus_out);
  or or_2 (or_2_out, signed_overflow_8bits_sub_1_minus_out, signed_overflow_8bits_sub_2_minus_out);
  Multiplexer #(.select(4)) multiplexer_1 (
    .in0(signed_overflow_16bits_add_1_plus_out), .in1(signed_overflow_16bits_sub_1_minus_out), .in2(1'b0),
    .in3(1'b0), .in4(1'b0), .in5(1'b0), .in6(1'b0), .in7(1'b0), .in8(or_1_out), .in9(or_2_out),
    .out(signed_overflow), .sel(Switch));  // open: in10, in11, in12, in13, in14, in15, en

  // Other names for the same wires on the sheet: X_7_0[7:0] = in_5; X_15_8[7:0] = in_7; Y_7_0[7:0] = in_6;
  //   Y_15_8[7:0] = in_9

  // Notes on the sheet:
  //   R-add
  //   R-sub
  //   addp8[7:0]
  //   addp8[15:8]
  //   subp8[7:0]
  //   subp8[15:8]
endmodule

module Signed_Overflow_16bits_Add (
  input  [15:0] in_1,
  input  [15:0] in_2,
  input  [15:0] in_3,
  output plus_out
);

  wire not_1_out, not_2_out, not_3_out, plus_case1, plus_case2;

  // Probe on in_1
  // Probe on in_2
  // Probe on in_3
  not not_1 (not_1_out, in_1[15]);
  not not_2 (not_2_out, in_2[15]);
  not not_3 (not_3_out, in_3[15]);
  and and_1 (plus_case1, not_1_out, in_3[15], not_2_out);
  and and_2 (plus_case2, in_1[15], not_3_out, in_2[15]);
  or or_1 (plus_out, plus_case1, plus_case2);

  // Other names for the same wires on the sheet: X_15 = in_1[15]; Y_15 = in_2[15]; R_15 = in_3[15]

  // Notes on the sheet:
  //   X
  //   Y
  //   result
  //   X and Y are positive, but R is negative
  //   X and Y are negative, but R is positive
endmodule

module Signed_Overflow_8bits_Add (
  input  [7:0] in_1,
  input  [7:0] in_2,
  input  [7:0] in_3,
  output plus_out
);

  wire not_1_out, not_2_out, not_3_out, plus_case1, plus_case2;

  // Probe on in_1
  // Probe on in_2
  // Probe on in_3
  not not_1 (not_1_out, in_1[7]);
  not not_2 (not_2_out, in_2[7]);
  not not_3 (not_3_out, in_3[7]);
  and and_1 (plus_case1, not_1_out, in_3[7], not_2_out);
  and and_2 (plus_case2, in_1[7], not_3_out, in_2[7]);
  or or_1 (plus_out, plus_case1, plus_case2);

  // Other names for the same wires on the sheet: X_7 = in_1[7]; Y_7 = in_2[7]; R_7 = in_3[7]

  // Notes on the sheet:
  //   X
  //   Y
  //   result
  //   X and Y are positive, but R is negative
  //   X and Y are negative, but R is positive
endmodule

module Signed_Overflow_16bits_Sub (
  input  [15:0] in_1,
  input  [15:0] in_2,
  input  [15:0] in_3,
  output minus_out
);

  wire minus_case1, minus_case2, not_1_out, not_2_out, not_3_out;

  // Probe on in_1
  // Probe on in_2
  // Probe on in_3
  not not_1 (not_1_out, in_3[15]);
  not not_2 (not_2_out, in_2[15]);
  not not_3 (not_3_out, in_1[15]);
  and and_1 (minus_case1, in_1[15], not_1_out, not_2_out);
  and and_2 (minus_case2, not_3_out, in_3[15], in_2[15]);
  or or_1 (minus_out, minus_case1, minus_case2);

  // Other names for the same wires on the sheet: X_15 = in_1[15]; Y_15 = in_2[15]; R_15 = in_3[15]

  // Notes on the sheet:
  //   X
  //   Y
  //   result
  //   X is negative, Y is positive, but R is positive
  //   X is positive, Y is negative, but R is negative
endmodule

module Signed_Overflow_8bits_Sub (
  input  [7:0] in_1,
  input  [7:0] in_2,
  input  [7:0] in_3,
  output minus_out
);

  wire minus_case1, minus_case2, not_1_out, not_2_out, not_3_out;

  // Probe on in_1
  // Probe on in_2
  // Probe on in_3
  not not_1 (not_1_out, in_3[7]);
  not not_2 (not_2_out, in_2[7]);
  not not_3 (not_3_out, in_1[7]);
  and and_1 (minus_case1, in_1[7], not_1_out, not_2_out);
  and and_2 (minus_case2, not_3_out, in_3[7], in_2[7]);
  or or_1 (minus_out, minus_case1, minus_case2);

  // Other names for the same wires on the sheet: X_7 = in_1[7]; Y_7 = in_2[7]; R_7 = in_3[7]

  // Notes on the sheet:
  //   X
  //   Y
  //   result
  //   X is negative, Y is positive, but R is positive
  //   X is positive, Y is negative, but R is negative
endmodule
