// Logisim project cpu.circ as structural Verilog: 2 circuits, main circuit main
module main (
  input  [15:0] From_Instr_Mem,
  input  clk,
  output [15:0] r0,
  output [15:0] r1,
  output [15:0] r2,
  output [15:0] r3,
  output [15:0] Display_0,
  output [15:0] Display_1,
  output [15:0] To_Instr_Mem,
  output [15:0] Data_Mem_Data,
  output [15:0] Data_Mem_Addr,
  output Data_Mem_Write
);

  wire ALUsrc, and_2_out, and_3_out, button_1_out, comparator_1_eq, disp_sel, Display, Equals, ExtOp, jal,
       kill, lui, main_2_signed_overflow, MemToReg, not_2_out, not_3_out, RegDst, RegWr;
  wire [1:0] multiplexer_4_out, multiplexer_5_out, nPC_sel, nPC_sel_q;
  wire [3:0] ALUctr;
  wire [5:1] funct;
  wire [7:6] imm;
  wire [15:0] adder_1_out, adder_2_out, Address, and_1_out, bit_extender_1_out, bit_extender_2_out,
       branchImm, DataIn, DataOut, demultiplexer_1_out0, demultiplexer_1_out1, IF_EX_Instr_q, jumpAddr,
       main_1_read_data_1, multiplexer_1_out, multiplexer_3_out, multiplexer_7_out, multiplexer_8_out,
       multiplexer_9_out, multiplexer_10_out, multiplexer_12_out, multiplexer_13_out, or_1_out;
  wire [15:8] Instr;

  Adder #(.width(16)) adder_1 (.a(16'h1), .b(To_Instr_Mem), .out(adder_1_out));  // open: cin, cout
  Register #(.width(2)) u_nPC_sel (.D(nPC_sel), .Q(nPC_sel_q), .clk(clk));  // open: en, clr
  Adder #(.width(16)) adder_2 (.a(To_Instr_Mem), .b(branchImm), .out(adder_2_out));  // open: cin, cout
  not not_1 (kill, comparator_1_eq);
  Comparator #(.width(2)) comparator_1 (.a(nPC_sel_q), .b(2'b00), .eq(comparator_1_eq));  // open: gt, lt
  Register #(.width(16)) IF_EX_Instr (.D(From_Instr_Mem), .Q(IF_EX_Instr_q), .clk(clk));  // open: en, clr
  Multiplexer #(.select(2), .width(16)) multiplexer_1 (
    .in0(adder_1_out), .in1(adder_2_out), .in2(jumpAddr), .out(multiplexer_1_out), .sel(nPC_sel));  // open: in3, en
  Register #(.width(16)) PC (.D(multiplexer_1_out), .Q(To_Instr_Mem), .clk(clk));  // open: en, clr
  Multiplexer #(.width(16)) multiplexer_2 (
    .in0(IF_EX_Instr_q), .in1(16'h6), .out({Instr, imm, funct, disp_sel}), .sel(kill));  // open: en
  Multiplexer #(.width(16)) multiplexer_3 (
    .in0(multiplexer_12_out), .in1(To_Instr_Mem), .out(multiplexer_3_out), .sel(jal));  // open: en
  Multiplexer #(.width(2)) multiplexer_4 (
    .in0(Instr[9:8]), .in1(imm), .out(multiplexer_4_out), .sel(RegDst));  // open: en
  Multiplexer #(.width(2)) multiplexer_5 (
    .in0(multiplexer_4_out), .in1(2'b11), .out(multiplexer_5_out), .sel(jal));  // open: en
  Regfile_main main_1 (
    .Read_register_1(Instr[11:10]), .Read_register_2(Instr[9:8]), .write_register(multiplexer_5_out),
    .write_data(multiplexer_3_out), .Reg_0_Value(r0), .Reg_1_Value(r1), .Reg_2_Value(r2), .Reg_3_Value(r3),
    .RegWrite(RegWr), .clock(clk), .Read_Data_1(main_1_read_data_1), .Read_Data_2(DataIn));
  assign bit_extender_1_out = {{8{1'b0}}, {imm, funct, disp_sel}};  // Bit_Extender bit_extender_1
  Multiplexer #(.width(16)) multiplexer_6 (
    .in0(bit_extender_1_out), .in1(bit_extender_2_out), .out(branchImm), .sel(ExtOp));  // open: en
  assign bit_extender_2_out = {{8{imm[7]}}, {imm, funct, disp_sel}};  // Bit_Extender bit_extender_2
  assign and_1_out = To_Instr_Mem & 16'hf000;  // AND_Gate and_1, 16 bits wide
  Multiplexer #(.width(16)) multiplexer_7 (
    .in0(DataIn), .in1(branchImm), .out(multiplexer_7_out), .sel(ALUsrc));  // open: en
  assign or_1_out = and_1_out | {4'b0000, Instr[11:8], imm, funct, disp_sel};  // OR_Gate or_1, 16 bits wide
  Multiplexer #(.select(2), .width(16)) multiplexer_8 (
    .in0(r0), .in1(r1), .in2(r2), .in3(r3), .out(multiplexer_8_out), .sel(Instr[11:10]));  // open: en
  Comparator #(.width(4)) comparator_2 (.a(Instr[15:12]), .b(4'b0001), .eq(jal));  // open: gt, lt
  Comparator #(.width(4)) comparator_3 (.a(Instr[15:12]), .b(4'b1010), .eq(lui));  // open: gt, lt
  Multiplexer #(.width(16)) multiplexer_9 (
    .in0(main_1_read_data_1), .in1(multiplexer_7_out), .out(multiplexer_9_out), .sel(lui));  // open: en
  alu_main main_2 (
    .Switch__S(ALUctr), .X(multiplexer_9_out), .Equal(Equals), .RESULT(Address),
    .Signed_Overflow(main_2_signed_overflow), .Y(multiplexer_10_out));
  Multiplexer #(.width(16)) multiplexer_10 (
    .in0(multiplexer_7_out), .in1(16'h8), .out(multiplexer_10_out), .sel(lui));  // open: en
  Multiplexer #(.select(4), .width(16)) multiplexer_11 (
    .in1(or_1_out), .in2(or_1_out), .in3(multiplexer_8_out), .out(jumpAddr), .sel(Instr[15:12]));  // open: in0, in4, in5, in6, in7, in8, in9, in10, in11, in12, in13, in14, in15, en
  LED led_1 (.in(main_2_signed_overflow));
  Hex_Digit_Display hex_digit_display_1 (.value(Display_0[15:12]));  // open: dp
  Multiplexer #(.width(16)) multiplexer_12 (
    .in0(Address), .in1(DataOut), .out(multiplexer_12_out), .sel(MemToReg));  // open: en
  Hex_Digit_Display hex_digit_display_2 (.value(Display_0[7:4]));  // open: dp
  Hex_Digit_Display hex_digit_display_3 (.value(Display_0[11:8]));  // open: dp
  Multiplexer #(.select(2), .width(16)) multiplexer_13 (
    .in0(r0), .in1(r1), .in2(r2), .in3(r3), .out(multiplexer_13_out), .sel(Instr[11:10]));  // open: en
  Control control_1 (
    .opcode(Instr[15:12]), .funct({funct, disp_sel}), .in_3(Equals), .RegWr(RegWr), .RegDst(RegDst),
    .ExtOp(ExtOp), .ALUsrc(ALUsrc), .ALUctr(ALUctr), .MemToReg(MemToReg), .MemWr(Data_Mem_Write),
    .nPC_sel(nPC_sel), .Display(Display));
  Multiplexer #(.width(16)) multiplexer_14 (
    .in0(16'hbadd), .in1(DataIn), .out(Data_Mem_Data), .sel(Data_Mem_Write));  // open: en
  Multiplexer #(.width(16)) multiplexer_15 (
    .in0(16'hbadd), .in1(Address), .out(Data_Mem_Addr), .sel(Data_Mem_Write));  // open: en
  Hex_Digit_Display hex_digit_display_4 (.value(Display_0[3:0]));  // open: dp
  Demultiplexer #(.width(16)) demultiplexer_1 (
    .out0(demultiplexer_1_out0), .out1(demultiplexer_1_out1), .in(multiplexer_13_out), .sel(disp_sel));  // open: en
  not not_2 (not_2_out, Data_Mem_Write);
  Hex_Digit_Display hex_digit_display_5 (.value(Display_1[11:8]));  // open: dp
  Hex_Digit_Display hex_digit_display_6 (.value(Display_1[15:12]));  // open: dp
  Register #(.width(16)) register_1 (.D(demultiplexer_1_out0), .en(and_2_out), .Q(Display_0), .clk(clk));  // open: clr
  Register #(.width(16)) register_2 (.D(demultiplexer_1_out1), .en(and_3_out), .Q(Display_1), .clk(clk));  // open: clr
  assign DataOut = Data_Mem_Write ? DataIn : 16'bz;  // Controlled_Buffer controlled_buffer_1
  RAM #(.addrWidth(16), .dataWidth(16)) ram_1 (
    .addr(Address), .data(DataOut), .sel(1'b1), .clk(clk), .ld(not_2_out), .clr(button_1_out));
  Button button_1 (.out(button_1_out));
  Hex_Digit_Display hex_digit_display_7 (.value(Display_1[3:0]));  // open: dp
  Hex_Digit_Display hex_digit_display_8 (.value(Display_1[7:4]));  // open: dp
  and and_2 (and_2_out, Display, not_3_out);
  and and_3 (and_3_out, disp_sel, Display);
  // Probe on DataOut
  not not_3 (not_3_out, disp_sel);

  // Other names for the same wires on the sheet: funct[0] = disp_sel; imm[5:0] = {funct, disp_sel};
  //   Instr[7:0] = {imm, funct, disp_sel}; rd[1:0] = imm; rt[1:0] = Instr[9:8]; rs[1:0] = Instr[11:10];
  //   d0[15:0] = Display_0; d1[15:0] = Display_1; MemWrite = Data_Mem_Write; currPC[15:0] = To_Instr_Mem;
  //   nextPC[15:0] = To_Instr_Mem; opcode[3:0] = Instr[15:12]

  // Notes on the sheet:
  //   This is the current PC that you need to send as OUTPUT
  //   This is the instruction that you would receive as INPUT
  //   DATAPATH
  //   This is a CLK that is an INPUT driven from the harness.
  //   Remember, this circuit is loaded from the harness to be tested!
  //   DO NOT CHANGE THE LOCATIONS OF THE INPUTS OR OUTPUTS! IF YOU DO SO, YOU NEED TO MAKE SURE THE PINS ARE IN THE RIGHT PLACES!
  //   These are OUTPUTS of the circuit
  //   INSTRUCTION DECODING
  //   JAL
  //   Signed Overflow Light
  //   CONTROL
  //   DISPLAY
  //   DATA MEMORY
  //   These are OUTPUTS of the circuit
endmodule

module Control (
  input  [3:0] opcode,
  input  [5:0] funct,
  input  in_3,
  output RegWr,
  output RegDst,
  output ExtOp,
  output ALUsrc,
  output [3:0] ALUctr,
  output MemToReg,
  output MemWr,
  output [1:0] nPC_sel,
  output Display
);

  wire addi_out, and_1_out, and_2_out, andi_out, beq, bne, branch, j_out, jal_out, jr_out, lui_out,
       not_1_out, not_2_out, not_3_out, not_4_out, not_5_out, ori_out;
  wire [1:0] multiplexer_2_out;

  not not_1 (not_1_out, opcode[3]);
  not not_2 (not_2_out, opcode[2]);
  not not_3 (not_3_out, opcode[1]);
  not not_4 (not_4_out, opcode[0]);
  and R (RegDst, not_1_out, not_2_out, not_3_out, not_4_out);
  and jal (jal_out, not_1_out, not_2_out, not_3_out, opcode[0]);
  and j (j_out, not_1_out, not_2_out, opcode[1], not_4_out);
  and jr (jr_out, not_1_out, not_2_out, opcode[1], opcode[0]);
  and u_beq (beq, not_1_out, opcode[2], not_3_out, not_4_out);
  and addi (addi_out, not_1_out, opcode[2], not_3_out, opcode[0]);
  and andi (andi_out, not_1_out, opcode[2], opcode[1], not_4_out);
  and ori (ori_out, not_1_out, opcode[2], opcode[1], opcode[0]);
  and u_bne (bne, opcode[3], not_2_out, not_3_out, not_4_out);
  and sw (MemWr, opcode[3], not_2_out, not_3_out, opcode[0]);
  and lui (lui_out, opcode[3], not_2_out, opcode[1], not_4_out);
  and lw (MemToReg, opcode[3], not_2_out, opcode[1], opcode[0]);
  and disp (Display, opcode[3], opcode[2], not_3_out, not_4_out);
  or or_1 (RegWr, RegDst, jal_out, addi_out, MemToReg, andi_out, ori_out, lui_out);
  or or_2 (ExtOp, beq, addi_out, bne, MemWr, MemToReg);
  or or_3 (ALUsrc, addi_out, andi_out, ori_out, MemWr, lui_out, MemToReg);
  Multiplexer #(.select(4), .width(4)) multiplexer_1 (
    .in0(funct[3:0]), .in1(4'b0000), .in2(4'b0000), .in3(4'b0000), .in4(4'b0000), .in5(4'b0000),
    .in6(4'b0111), .in7(4'b0110), .in8(4'b0000), .in9(4'b0000), .in10(4'b0010), .in11(4'b0000),
    .in12(4'b0000), .out(ALUctr), .sel(opcode));  // open: in13, in14, in15, en
  Multiplexer #(.width(2)) multiplexer_2 (.in0(2'b00), .in1(2'b01), .out(multiplexer_2_out), .sel(branch));  // open: en
  and and_1 (and_1_out, beq, in_3);
  and and_2 (and_2_out, bne, not_5_out);
  not not_5 (not_5_out, in_3);
  Multiplexer #(.select(4), .width(2)) multiplexer_3 (
    .in0(2'b00), .in1(2'b10), .in2(2'b10), .in3(2'b10), .in4(multiplexer_2_out), .in5(2'b00), .in6(2'b00),
    .in7(2'b00), .in8(multiplexer_2_out), .in9(2'b00), .in10(2'b00), .in11(2'b00), .in12(2'b00),
    .out(nPC_sel), .sel(opcode));  // open: in13, in14, in15, en
  or or_4 (branch, and_1_out, and_2_out);

  // Other names for the same wires on the sheet: ALUop[3:0] = ALUctr; Equals = in_3; op0 = opcode[0]; op1 = opcode[1];
  //   op2 = opcode[2]; op3 = opcode[3]

  // Notes on the sheet:
  //   INPUTS TO CONTROL
endmodule
